# Fritzing sketch liana_rangkaian (saved by Fritzing 0.9.2b)

parts:
  Conductivity_Circuit1 = Conductivity Circuit
  Part1 = Arduino Mega 2560 (Rev3)
  WATER_PUMP2 = water pump/motor
  LED1 = LEDs [package=led10mm]
  U1 = Module 4 Relais 5V [package="Module 4 Relais 5V"]
  U2 = NodeMCU V3.0
  ZS-042_RTC1 = ZS-042 RTC Module
  DFPlayer_Mini1 = DFPlayer MINI [package="DIP (Dual Inline) [THT]"]
  SP1 = SPEAKER [package=pcb_mount_speaker]
  Display1 = LCD screen 16x2 IIC [part_number=101290]
  Part2 = SRF05 Ultrasonic Rangefinder
  DS1 = DS18B20 1-Wire Temperature Sensor Probe Cable
  S1 = PH meter [package=THT]
  LED2 = LEDs [package=led10mm]
  WATER_PUMP3 = water pump/motor
  WATER_PUMP4 = water pump/motor
  LED3 = LEDs [package=led10mm]
  LED4 = LEDs [package=led10mm]  # not connected
  LED5 = LEDs [package=led10mm]

nets:
  GND: Conductivity_Circuit1.GND, Part1.GND, U1.GND, U2.GND, ZS-042_RTC1.GND, DFPlayer_Mini1.GND, Display1.GND, Part2.GND, DS1.GND, S1.pin3, LED3.A, LED5.A
  VCC: Conductivity_Circuit1.TX, Part1.5V, U1.VCC, DFPlayer_Mini1.VCC, Display1.VCC, Part2.VCC, DS1.VDD, S1.pin2
  N1: Conductivity_Circuit1.RX, Part1.D53
  N2: Part1.A0, DS1.shield
  N3: Part1.A1, S1.pin1
  N4: Part1.D21/SCL, Part1.SCL, ZS-042_RTC1.SDA, Display1.SCL
  N5: Part1.D20/SDA, Part1.SDA, ZS-042_RTC1.SCL, Display1.SDA
  N6: Part1.D19/RX1, U2.D1
  N7: Part1.D18/TX1, U2.D2
  N8: Part1.D23, U1.IN1
  N9: Part1.D25, U1.IN2
  N10: Part1.D27, U1.IN3
  N11: Part1.D29, U1.IN4
  N12: Part1.D31, Part2.Trig
  N13: Part1.D33, Part2.Echo
  N14: WATER_PUMP2.pin_2, U1.K3-NF
  N15: LED1.C, LED2.C
  N16: U1.K1-NF, WATER_PUMP4.pin_2
  N17: U1.K2-NF, WATER_PUMP3.pin_2
  N18: U1.K1-NO, U1.K4-NO
  N19: U2.D3, LED3.C
  N20: U2.D4, LED5.C
  N21: DFPlayer_Mini1.SPK1, SP1.-
  N22: DFPlayer_Mini1.SPK2, SP1.+

custom parts:
  water pump/motor: WATER PUMP BY ARDUBLOCKTR
  Module 4 Relais 5V: Module 4 Relais 5V 4x SPD-06VDC-SD-C
  NodeMCU V3.0: ESP8266 based NodeMCU
  DFPlayer MINI: MP3 module by DFRobot.com for playing Music from an SD-Card. Supports WAV and MP3 files.
  LCD screen 16x2 IIC: LCD screen with HD44780 controller enables showing text, symbols, value or anything else that comes from Croduino/Arduino. It is capable of showing 16 symbols in two lines and therefore can be used in many projects that need to send clearly visible and legible output information.. • Color of symbols: White • Backlight: Blue • Dimensions: 80 x 36 x 12 mm • Screen dimensions: 64.5 x 16 mm •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
